# Fritzing sketch BoostControler_proto (saved by Fritzing 0.9.3b)
circuit board: 8.46667cm x 5.64444cm
perfboards: 1

parts:
  Composant2 = Arduino Nano (Rev3.0)
  Q1 = NPN-Transistor [package="TO92 [THT]"]
  Q2 = npn-Powertransistor [package="TO220 [THT]"]
  R1 = Resistor [tolerance=±5% resistance=1k package=THT]
  U1 = Voltage Regulator - 5V [package="TO220 [THT]"]
  U2 = TVS [package=sma-diode]
  C1 = Electrolytic Capacitor [capacitance=1µF voltage=20V package="100 mil [THT, electrolytic]"]
  C2 = Electrolytic Capacitor [capacitance=0.1µF voltage=10V package="100 mil [THT, electrolytic]"]
  J2 = male pin header, 5 pins [form="♂ (male)"]
  J3 = male pin header, 2 pins [form="♂ (male)"]
  J4 = male pin header, 2 pins [form="♂ (male)"]
  Composant3 = Bluetooth HC-05 Macho
  R2 = Resistor [tolerance=±5% resistance=4k package=THT]
  R3 = Resistor [tolerance=±5% resistance=1k package=THT]
  R4 = Resistor [tolerance=±5% resistance=2k package=THT]
  R5 = Resistor [tolerance=±5% resistance=10k package=THT]
  R6 = Resistor [tolerance=±5% resistance=10k package=THT]
  R7 = Resistor [tolerance=±5% resistance=2k package=THT]
  R8 = Resistor [tolerance=±5% resistance=1k package=THT]
  Q3 = NPN-Transistor [package="TO92 [THT]"]

nets:
  N1: Composant2.D1/TX, R8.Pin_0
  N2: Composant2.D0/RX, R6.Pin_1, Q3.C
  GND: Composant2.GND, Q2.emitter, U1.GND, U2.1, C1.-, C2.-, J2.pin2, J3.pin2, Composant3.GND, R4.Pin_1, R7.Pin_1
  AIR_FLOW_HZ: Composant2.D10, J4.pin2
  N3: Composant2.D11/MOSI, J2.pin4
  RPM: Composant2.D12/MISO, J2.pin3
  5V: Composant2.VIN, U1.output_voltage, C2.+, Composant3.VCC, R3.Pin_0, R6.Pin_0
  N4: Composant2.A5, J2.pin5
  MAP: Composant2.A4, J3.pin1
  N5: Composant2.D13/SCK, R1.Pin_0
  N6: Q1.E, Q2.base
  N7: Q1.B, R1.Pin_1
  WG_SOL: Q1.C, Q2.collector, J4.pin1
  12V: U1.input_voltage, U2.2, C1.+, J2.pin1
  N8: Composant3.TXD, R7.Pin_0, R8.Pin_1
  N9: Composant3.RXD, R5.Pin_1, Q3.E
  N10: R2.Pin_0, Q3.B
  3.3V: R2.Pin_1, R3.Pin_1, R4.Pin_0, R5.Pin_0
