# Fritzing sketch Simulateur (saved by Fritzing 0.9.3b)
perfboards: 1

parts:
  Composant1 = Arduino Nano (Rev3.0) (ICSP)
  WG = LED - 3mm [color="Red (660nm)" package="3 mm [THT]"]
  F_PUMP = LED - 3mm [color="Red (633nm)" package="3 mm [THT]"]
  U1 = POT [package=pot_alpha_rv16af-20]
  U2 = POT [package=pot_alpha_rv16af-20]
  U3 = POT [package=pot_alpha_rv16af-20]
  R1 = Resistor [tolerance=±5% resistance=220 package=THT]
  R2 = Resistor [tolerance=±5% resistance=220 package=THT]
  J1 = rounded female pin header, 5 pins [form="♀ (female rounded)"]
  J3 = rounded female pin header, 3 pins [form="♀ (female rounded)"]
  J2 = rounded female pin header, 4 pins [form="♀ (female rounded)"]
  SPEED- = Pushbutton [package="[THT]"]
  SPEED+ = Pushbutton [package="[THT]"]
  R3 = Resistor [tolerance=±5% resistance=10k package="1206 [SMD]"]
  R4 = Resistor [tolerance=±5% resistance=3.3k package="1206 [SMD]"]
  Q1 = TRANSISTOR_NPN [package=to-92]
  R5 = Resistor [tolerance=±5% resistance=220 package="1206 [SMD]"]
  L1 = Inductor [package="1206 [SMD]"]
  D1 = Diode [package=diode-hv]
  C1 = Capacitor Polarized [package=cpol-radial-10uf-25v]
  C2 = Capacitor Polarized [package=cpol-radial-10uf-25v]
  C3 = Ceramic Capacitor [capacitance="100 nF" package="1206 [SMD, multilayer]"]

nets (from the schematic view):
  GND: Composant1.GND, U1.A, U2.A, U3.A, J1.pin2, J2.pin2, J2.pin4, SPEED-.Pin_1, SPEED-.Pin_2, SPEED+.Pin_1, SPEED+.Pin_2, R4.Pin_1, Q1.E, C1.-, C2.-, C3.0
  N1: Composant1.D3, R5.Pin_0
  N2: Composant1.D7, SPEED+.Pin_3, SPEED+.Pin_4
  N3: Composant1.D8, SPEED-.Pin_3, SPEED-.Pin_4
  MAF: Composant1.D11/MOSI, J3.pin2
  SPEED: Composant1.D12/MISO, J1.pin4
  5V: Composant1.5V, U1.E, U2.E, U3.E, R1.Pin_0, R2.Pin_0, L1.pin_0, C2.+, C3.1
  N4: Composant1.A1, R3.Pin_1, R4.Pin_0
  RPM: Composant1.D13/SCK, J1.pin3
  N5: WG.cathode, J3.pin1
  N6: WG.anode, R1.Pin_1
  N7: F_PUMP.cathode, J3.pin3
  N8: F_PUMP.anode, R2.Pin_1
  N9: U1.S, J2.pin1
  N10: U2.S, J1.pin5
  N11: U3.S, J2.pin3
  12V: J1.pin1, R3.Pin_0, D1.C, C1.+
  N12: Q1.B, R5.Pin_1
  N13: Q1.C, L1.pin_1, D1.A

notes:
  Voltage loopback
  Voltage booster
  THROTTLE
  F_PRES
  MAP
