# Fritzing sketch Wire_MAP_solenoid (saved by Fritzing 0.9.3b)
perfboards: 1

parts:
  Q1 = npn-Powertransistor [package="TO220 [THT]"]
  Q2 = NPN-Transistor [package="TO92 [THT]"]
  J1 = shrouded pin header, 8 pins [form="♂ (shrouded male)"]
  R1 = Resistor [tolerance=±5% resistance=220 package=THT]
  R2 = Resistor [tolerance=±5% resistance=1k package=THT]

nets:
  N1: Q1.base, Q2.C, R1.Pin_1
  N2: Q1.collector, J1.pin3
  GND: Q1.emitter, Q2.E, J1.pin4
  N3: Q2.B, J1.pin2, R2.Pin_1
  N4: J1.pin1, R1.Pin_0, R2.Pin_0

notes:
  R - VBat
  J - ECU Sol
  V - MAP Sol
  B - GND
